# Fritzing sketch KeyBlaster (saved by Fritzing 0.9.4)
breadboards: 1

parts:
  Bauteil1 = Arduino Micro (Rev3)
  Squix1 = OLED 0.96" 128x64 I2C SSD1306
  S1 = Pushbutton [package="[THT]"]
  S2 = Pushbutton [package="[THT]"]
  S3 = Pushbutton [package="[THT]"]

nets:
  N1: Bauteil1.RESET, Bauteil1.D8_PWM/A8
  GND: Bauteil1.GND, Squix1.GND, S1.Pin_3, S1.Pin_4, S2.Pin_3, S2.Pin_4, S3.Pin_3, S3.Pin_4
  N2: Bauteil1.D2/SDA, Squix1.SCA
  N3: Bauteil1.D3/SCL, Squix1.SCL
  N4: Bauteil1.D4_PWM/A6, S3.Pin_1, S3.Pin_2
  5V: Bauteil1.5V, Squix1.VCC
  N5: Bauteil1.A5, S1.Pin_1, S1.Pin_2
  N6: Bauteil1.A4, S2.Pin_1, S2.Pin_2
